# Fritzing sketch breathe (saved by Fritzing 0.9.2b)
breadboards: 1

parts:
  IC1 = DIP - 14 pins [chip_label=ATTiny24/44/84 package="DIP (Dual Inline) [THT]"]
  VCC1 = Battery
  R3 = Resistor [tolerance=±5% resistance=220 package="0805 [SMD]"]
  LED1 = LED - 5mm [color="Red (633nm)" package="5 mm [THT]"]

nets:
  N1: IC1.pin1, VCC1.+
  N2: IC1.pin12, LED1.anode
  N3: IC1.pin14, VCC1.-, R3.Pin_0
  N4: R3.Pin_1, LED1.cathode

custom parts:
  DIP - 14 pins: A DIP stand-in part for whatever IC you want. With 14 pins on a 300mil dual inline package (DIP) footprint.
