# Fritzing sketch rgb-lamp (saved by Fritzing 0.9.2b)
breadboards: 1

parts:
  IC1 = DIP - 14 pins [chip_label=ATTiny24/44/84 package="DIP (Dual Inline) [THT]"]
  LED1 = RGB LED (com. cathode, rbg) [package="5 mm [THT]"]
  VCC1 = Battery
  R1 = Resistor [tolerance=±5% resistance=220 package="0805 [SMD]"]
  R2 = Resistor [tolerance=±5% resistance=220 package="0805 [SMD]"]
  R3 = Resistor [tolerance=±5% resistance=220 package="0805 [SMD]"]

nets:
  N1: IC1.pin1, VCC1.+
  N2: IC1.pin5, R3.Pin_0
  N3: IC1.pin6, R2.Pin_0
  N4: IC1.pin7, R1.Pin_0
  N5: IC1.pin14, LED1.common_cathode, VCC1.-
  N6: LED1.red_anode, R3.Pin_1
  N7: LED1.blue_anode, R2.Pin_1
  N8: LED1.green_anode, R1.Pin_1

custom parts:
  DIP - 14 pins: A DIP stand-in part for whatever IC you want. With 14 pins on a 300mil dual inline package (DIP) footprint.
