# Fritzing sketch programming (saved by Fritzing 0.9.2b)
breadboards: 1

parts:
  IC1 = DIP - 14 pins [chip_label=ATTiny24/44/84 package="DIP (Dual Inline) [THT]"]
  J1 = AVR ISP 6 Pin [package=2x3]

nets:
  N1: IC1.pin1, J1.2
  N2: IC1.pin4, J1.5
  N3: IC1.pin7, J1.4
  N4: IC1.pin8, J1.1
  N5: IC1.pin9, J1.3
  N6: IC1.pin14, J1.6

notes:
  1 MISO white
  2 VCC red
  3 SCK orange
  4 MOSI green
  5 RST blue
  6 GND black

custom parts:
  DIP - 14 pins: A DIP stand-in part for whatever IC you want. With 14 pins on a 300mil dual inline package (DIP) footprint.
